// Logisim project alu.circ as structural Verilog: 1 circuit, main circuit arithmetic_logic_unit
module arithmetic_logic_unit (
  input  [7:0] A,
  input  [7:0] B,
  input  ADD,
  input  SUB,
  input  ANA,
  input  ORA,
  input  XRA,
  output CARRY,
  output SIGN,
  output [7:0] Q
);

  wire not_1_out;
  wire [7:0] adder_1_out, and_1_out, controlled_buffer_5_out, controlled_inverter_1_out, or_1_out,
       subtractor_1_out, xor_1_out;

  Adder adder_1 (.a(A), .b(B), .out(adder_1_out), .cout(CARRY));  // open: cin
  Subtractor subtractor_1 (.a(A), .b(B), .out(subtractor_1_out), .bout(SIGN));  // open: bin
  assign and_1_out = A & B;  // AND_Gate and_1, 8 bits wide
  assign or_1_out = A | B;  // OR_Gate or_1, 8 bits wide
  assign xor_1_out = A ^ B;  // XOR_Gate xor_1, 8 bits wide
  assign Q = ADD ? adder_1_out : 8'bz;  // Controlled_Buffer controlled_buffer_1
  assign controlled_inverter_1_out = SIGN ? ~subtractor_1_out : 8'bz;  // Controlled_Inverter controlled_inverter_1
  not not_1 (not_1_out, SIGN);
  assign Q = ANA ? and_1_out : 8'bz;  // Controlled_Buffer controlled_buffer_2
  assign Q = ORA ? or_1_out : 8'bz;  // Controlled_Buffer controlled_buffer_3
  assign Q = XRA ? xor_1_out : 8'bz;  // Controlled_Buffer controlled_buffer_4
  assign controlled_buffer_5_out = not_1_out ? subtractor_1_out : 8'bz;  // Controlled_Buffer controlled_buffer_5
  Adder adder_2 (.a(8'h1), .b(controlled_inverter_1_out), .out(controlled_buffer_5_out));  // open: cin, cout
  assign Q = SUB ? controlled_buffer_5_out : 8'bz;  // Controlled_Buffer controlled_buffer_6
endmodule
